# Fritzing sketch LEDStrip (saved by Fritzing 0.9.2b)
breadboards: 1

parts:
  Part1 = Arduino Uno (Rev3)
  LED1 = DUO LED RG [package="5 mm [THT]"]

nets:
  N1: Part1.D13/SCK, LED1.green_anode
  N2: Part1.3V3, LED1.red_anode
  N3: Part1.GND, LED1.common_cathode
