# Fritzing sketch Temperature (saved by Fritzing 0.9.2b)
breadboards: 1

parts:
  Part1 = Arduino Uno (Rev3)
  T1 = LM34 Temperature Sensor [package="TO92 [THT]"]
  R1 = Resistor [tolerance=±5% resistance=4.7k package=THT]

nets:
  N1: Part1.D2, T1.Vout, R1.Pin_0
  N2: Part1.3V3, R1.Pin_1
  GND: Part1.GND, T1.+Vs, T1.GND
